// Logisim project Led_7_doan.circ as structural Verilog: 1 circuit, main circuit main
module main (
  input  I0,
  input  I1,
  input  I2,
  input  I3
);

  wire and_1_out, and_2_out, and_3_out, and_4_out, and_5_out, and_6_out, and_7_out, and_8_out, and_9_out,
       and_10_out, and_11_out, and_12_out, and_13_out, and_14_out, and_15_out, and_16_out, and_17_out,
       and_18_out, and_19_out, and_20_out, and_21_out, and_22_out, and_23_out, and_24_out, and_25_out,
       and_26_out, and_27_out, and_28_out, and_29_out, and_30_out, and_31_out, and_32_out, and_33_out,
       and_34_out, and_35_out, and_36_out, and_37_out, and_38_out, D0_out, D1_out, D2_out, D3_out, D4_out,
       D5_out, D6_out, not_1_out, not_2_out, not_3_out, not_4_out;

  not not_1 (not_1_out, I0);
  not not_2 (not_2_out, I1);
  not not_3 (not_3_out, I2);
  not not_4 (not_4_out, I3);
  and and_1 (and_1_out, not_2_out, I3);
  and and_2 (and_2_out, not_1_out, not_3_out, not_4_out);
  and and_3 (and_3_out, not_3_out, not_4_out, I1);
  and and_4 (and_4_out, not_1_out, I1, I2);
  and and_5 (and_5_out, not_3_out, I0, I3);
  and and_6 (and_6_out, not_2_out, I0, I2);
  and and_7 (and_7_out, not_2_out, not_4_out);
  and and_8 (and_8_out, not_4_out, I0);
  and and_9 (and_9_out, not_4_out, I2);
  and and_10 (and_10_out, not_3_out, I3);
  and and_11 (and_11_out, not_2_out, I0);
  and and_12 (and_12_out, not_1_out, not_3_out);
  and and_13 (and_13_out, not_1_out, I1);
  and and_14 (and_14_out, I2, I3);
  and and_15 (and_15_out, I1, I3);
  and and_16 (and_16_out, not_3_out, I1);
  and and_17 (and_17_out, not_1_out, I1);
  and and_18 (and_18_out, not_3_out, I3);
  and and_19 (and_19_out, I0, I3);
  and and_20 (and_20_out, not_2_out, not_4_out, I2);
  and and_21 (and_21_out, not_3_out, not_4_out);
  and and_22 (and_22_out, not_1_out, not_3_out);
  and and_23 (and_23_out, not_2_out, not_3_out);
  and and_24 (and_24_out, not_1_out, not_2_out, not_4_out);
  and and_25 (and_25_out, not_4_out, I0, I1);
  and and_26 (and_26_out, not_2_out, I0, I3);
  and and_27 (and_27_out, not_1_out, not_2_out);
  and and_28 (and_28_out, not_3_out, I3);
  and and_29 (and_29_out, I1, I3);
  and and_30 (and_30_out, not_2_out, not_4_out, I2);
  and and_31 (and_31_out, not_1_out, I1, I2);
  and and_32 (and_32_out, not_1_out, not_3_out);
  and and_33 (and_33_out, not_1_out, I1);
  and and_34 (and_34_out, not_4_out, I1);
  and and_35 (and_35_out, I1, I2);
  and and_36 (and_36_out, not_1_out, I3);
  and and_37 (and_37_out, not_2_out, not_3_out, I3);
  and and_38 (and_38_out, not_4_out, I0, I2);
  or D0 (D0_out, and_1_out, and_2_out, and_3_out, and_4_out, and_5_out, and_6_out);
  or D1 (D1_out, and_7_out, and_8_out, and_9_out, and_10_out, and_11_out);
  or D2 (D2_out, and_12_out, and_13_out, and_14_out, and_15_out);
  or D3 (D3_out, and_16_out, and_17_out, and_18_out, and_19_out, and_20_out);
  or D4 (D4_out, and_21_out, and_22_out, and_23_out, and_24_out, and_25_out, and_26_out);
  or D5 (D5_out, and_27_out, and_28_out, and_29_out, and_30_out, and_31_out);
  or D6 (D6_out, and_32_out, and_33_out, and_34_out, and_35_out, and_36_out, and_37_out, and_38_out);
  _7_Segment_Display u_7_segment_display_1 (
    .g(D3_out), .f(D5_out), .a(D6_out), .b(D4_out), .e(D2_out), .d(D0_out), .c(D1_out));  // open: dp
endmodule
